# Fritzing sketch edison_schematics (saved by Fritzing 0.9.3b)

parts:
  Part1 = Intel Edison Arduinobreakout
  USBTTL1 = USB TTL Serial Cable

nets:
  N1: Part1.D0/RX, USBTTL1.TX
  N2: Part1.D1/TX, USBTTL1.RX
  GND: Part1.GND, USBTTL1.GND
