# Fritzing sketch rpi3_schematics (saved by Fritzing 0.9.3b)

parts:
  USBTTL1 = USB TTL Serial Cable
  Raspberry_Pi_1 = Raspberry Pi 3 [part_number=RPI-3-V1.2]

nets:
  N1: USBTTL1.RX, Raspberry_Pi_1.GPIO14
  N2: USBTTL1.TX, Raspberry_Pi_1.GPIO15
  GND: USBTTL1.GND, Raspberry_Pi_1.GND
